// Logisim project JK Double FlipFlop with reset.circ as structural Verilog: 1 circuit, main circuit main
module main (
  input  Q_initial,
  input  in_2,
  input  in_3,
  input  in_4,
  output out_5,
  output out_6
);

  wire and_1_out, and_2_out, clock_1_out, nand_1_out, nand_2_out, nand_3_out, nand_4_out, nand_5_out,
       nand_6_out, nand_7_out, not_1_out, not_2_out;

  Clock clock_1 (.out(clock_1_out));
  nand nand_1 (nand_1_out, out_6, in_3, clock_1_out);
  nand nand_2 (nand_2_out, clock_1_out, in_4, out_5);
  not not_1 (not_1_out, clock_1_out);
  nand nand_3 (nand_3_out, nand_1_out, nand_4_out);
  nand nand_4 (nand_4_out, nand_3_out, nand_2_out);
  nand nand_5 (nand_5_out, nand_3_out, not_1_out);
  nand nand_6 (nand_6_out, not_1_out, nand_4_out);
  not not_2 (not_2_out, in_2);
  and and_1 (and_1_out, not_2_out, Q_initial);
  and and_2 (and_2_out, in_2, nand_7_out);
  nand nand_7 (nand_7_out, nand_5_out, out_6);
  nand nand_8 (out_6, out_5, nand_6_out);
  or or_1 (out_5, and_1_out, and_2_out);

  // Notes on the sheet:
  //   Click 0 to reset Q
endmodule
