// Logisim project RACING _ JK FlipFlop with Q reset.circ as structural Verilog: 1 circuit, main circuit main
module main (
  input  Q_initial,
  input  in_2,
  input  in_3,
  input  in_4,
  output out_5,
  output out_6
);

  wire and_1_out, and_2_out, clock_1_out, nand_1_out, nand_2_out, nand_3_out, not_1_out;

  Clock clock_1 (.out(clock_1_out));
  not not_1 (not_1_out, in_2);
  nand nand_1 (nand_1_out, out_6, in_3, clock_1_out);
  nand nand_2 (nand_2_out, clock_1_out, in_4, out_5);
  and and_1 (and_1_out, not_1_out, Q_initial);
  and and_2 (and_2_out, in_2, nand_3_out);
  nand nand_3 (nand_3_out, nand_1_out, out_6);
  nand nand_4 (out_6, out_5, nand_2_out);
  or or_1 (out_5, and_1_out, and_2_out);

  // Notes on the sheet:
  //   Set Both Inputs as 1 for Racing
  //   Click 0 to reset Q
endmodule
