// Logisim project RACING _ T FlipFlop.circ as structural Verilog: 1 circuit, main circuit main
module main (
  input  Q_initial,
  input  in_2,
  input  T,
  output out_4,
  output out_5
);

  wire and_1_out, and_2_out, clock_1_out, nand_1_out, nand_2_out, nand_3_out, not_1_out;

  Clock clock_1 (.out(clock_1_out));
  nand nand_1 (nand_1_out, out_5, T, clock_1_out);
  nand nand_2 (nand_2_out, clock_1_out, T, out_4);
  not not_1 (not_1_out, in_2);
  and and_1 (and_1_out, not_1_out, Q_initial);
  and and_2 (and_2_out, in_2, nand_3_out);
  nand nand_3 (nand_3_out, nand_1_out, out_5);
  nand nand_4 (out_5, out_4, nand_2_out);
  or or_1 (out_4, and_1_out, and_2_out);

  // Notes on the sheet:
  //   Click 0 to reset Q
endmodule
