// Logisim project SLOWING CLOCK _ Multiple JK Slave FlipFlop.circ as structural Verilog: 1 circuit, main circuit main
module main (
  input  Q_initial,
  input  in_2,
  input  in_3,
  input  Q_initial_2,
  input  in_5,
  input  in_6,
  input  Q_initial_3,
  input  in_8,
  input  in_9,
  output out_10,
  output out_11,
  output out_12,
  output out_13,
  output out_14,
  output out_15,
  output minus_50,
  output minus_50_2,
  output CLOCK_3,
  output minus_50_3,
  output minus_50_4,
  output CLOCK_3_2,
  output minus_50_5,
  output minus_50_6,
  output CLOCK_3_3,
  output minus_50_7,
  output minus_50_8,
  output CLOCK_3_4
);

  wire and_1_out, and_2_out, and_3_out, and_4_out, and_5_out, and_6_out, nand_1_out, nand_2_out, nand_3_out,
       nand_4_out, nand_5_out, nand_6_out, nand_7_out, nand_9_out, nand_10_out, nand_11_out, nand_12_out,
       nand_13_out, nand_14_out, nand_15_out, nand_16_out, nand_17_out, nand_18_out, nand_19_out,
       nand_20_out, nand_21_out, nand_23_out, not_1_out, not_2_out, not_3_out, not_4_out, not_5_out,
       not_6_out;

  Clock clock_1 (.out(minus_50));
  nand nand_1 (nand_1_out, minus_50_4, in_6, minus_50);
  nand nand_2 (nand_2_out, minus_50, in_6, minus_50_2);
  not not_1 (not_1_out, minus_50);
  nand nand_3 (nand_3_out, nand_1_out, nand_4_out);
  nand nand_4 (nand_4_out, nand_3_out, nand_2_out);
  nand nand_5 (nand_5_out, nand_3_out, not_1_out);
  nand nand_6 (nand_6_out, not_1_out, nand_4_out);
  not not_2 (not_2_out, in_5);
  and and_1 (and_1_out, not_2_out, Q_initial_2);
  and and_2 (and_2_out, in_5, nand_7_out);
  nand nand_7 (nand_7_out, nand_5_out, minus_50_4);
  nand nand_8 (minus_50_4, minus_50_2, nand_6_out);
  or or_1 (minus_50_2, and_1_out, and_2_out);
  nand nand_9 (nand_9_out, CLOCK_3_3, in_3, minus_50_2);
  nand nand_10 (nand_10_out, minus_50_2, in_3, CLOCK_3);
  not not_3 (not_3_out, minus_50_2);
  nand nand_11 (nand_11_out, CLOCK_3_4, in_9, minus_50_4);
  nand nand_12 (nand_12_out, minus_50_4, in_9, CLOCK_3_2);
  not not_4 (not_4_out, minus_50_4);
  nand nand_13 (nand_13_out, nand_9_out, nand_14_out);
  nand nand_14 (nand_14_out, nand_13_out, nand_10_out);
  nand nand_15 (nand_15_out, nand_11_out, nand_16_out);
  nand nand_16 (nand_16_out, nand_15_out, nand_12_out);
  nand nand_17 (nand_17_out, nand_13_out, not_3_out);
  nand nand_18 (nand_18_out, not_3_out, nand_14_out);
  not not_5 (not_5_out, in_2);
  not not_6 (not_6_out, in_8);
  nand nand_19 (nand_19_out, nand_15_out, not_4_out);
  nand nand_20 (nand_20_out, not_4_out, nand_16_out);
  and and_3 (and_3_out, not_5_out, Q_initial);
  and and_4 (and_4_out, in_2, nand_21_out);
  nand nand_21 (nand_21_out, nand_17_out, CLOCK_3_3);
  nand nand_22 (CLOCK_3_3, CLOCK_3, nand_18_out);
  and and_5 (and_5_out, not_6_out, Q_initial_3);
  and and_6 (and_6_out, in_8, nand_23_out);
  nand nand_23 (nand_23_out, nand_19_out, CLOCK_3_4);
  nand nand_24 (CLOCK_3_4, CLOCK_3_2, nand_20_out);
  or or_2 (CLOCK_3, and_3_out, and_4_out);
  or or_3 (CLOCK_3_2, and_5_out, and_6_out);

  assign minus_50_3 = minus_50;
  assign minus_50_5 = minus_50;
  assign minus_50_6 = minus_50_2;
  assign minus_50_7 = minus_50;
  assign minus_50_8 = minus_50_4;
  assign out_10 = CLOCK_3;
  assign out_11 = CLOCK_3_3;
  assign out_12 = minus_50_2;
  assign out_13 = minus_50_4;
  assign out_14 = CLOCK_3_2;
  assign out_15 = CLOCK_3_4;

  // Notes on the sheet:
  //   Click 0 to reset Q
  //   CLOCK 1
  //   CLOCK 1
  //   CLOCK 2
  //   CLOCK 2
  //   Slowing Down a Clock
  //   CLOCK 1
  //   CLOCK 1
  //   CLOCK 2
  //   CLOCK 2
  //   Click 0 to reset Q
  //   Click 0 to reset Q
endmodule
