// Logisim project Universal Register.circ as structural Verilog: 1 circuit, main circuit main
module main (
  input  [1:0] _1_1___Left_Shift,
  input  in_2,
  input  Left_Shift_Input,
  input  in_4,
  input  in_5,
  input  in_6,
  input  in_7,
  output out_8,
  output out_9,
  output out_10,
  output out_11
);

  wire clock_1_out, multiplexer_1_out, multiplexer_2_out, multiplexer_3_out, multiplexer_4_out;

  Clock clock_1 (.out(clock_1_out));
  Multiplexer #(.select(2)) multiplexer_1 (
    .in0(in_2), .in1(in_4), .in2(out_8), .in3(out_9), .out(multiplexer_1_out), .sel(_1_1___Left_Shift));  // open: en
  D_Flip_Flop d_ff_1 (.clk(clock_1_out), .D(multiplexer_1_out), .Q(out_8));  // open: Qn, preset, en, reset
  Multiplexer #(.select(2)) multiplexer_2 (
    .in0(out_8), .in1(in_5), .in2(out_9), .in3(out_10), .out(multiplexer_2_out), .sel(_1_1___Left_Shift));  // open: en
  D_Flip_Flop d_ff_2 (.clk(clock_1_out), .D(multiplexer_2_out), .Q(out_9));  // open: Qn, preset, en, reset
  Multiplexer #(.select(2)) multiplexer_3 (
    .in0(out_9), .in1(in_6), .in2(out_10), .in3(out_11), .out(multiplexer_3_out), .sel(_1_1___Left_Shift));  // open: en
  D_Flip_Flop d_ff_3 (.clk(clock_1_out), .D(multiplexer_3_out), .Q(out_10));  // open: Qn, preset, en, reset
  D_Flip_Flop d_ff_4 (.clk(clock_1_out), .D(multiplexer_4_out), .Q(out_11));  // open: Qn, preset, en, reset
  Multiplexer #(.select(2)) multiplexer_4 (
    .in0(out_10), .in1(in_7), .in2(out_11), .in3(Left_Shift_Input), .out(multiplexer_4_out),
    .sel(_1_1___Left_Shift));  // open: en

  // Notes on the sheet:
  //   0 0 : Right Shift
  //   0 1 : Parallel Input
  //   1 0 : Buffer
  //   Right Shift Input
  //   Parallel Inputs
endmodule
