// Logisim project (tbd)MODIFIED LIMITED COUNTER.circ as structural Verilog: 1 circuit, main circuit main
module main (
  input  A,
  input  in_2,
  input  in_3,
  input  in_4,
  input  in_5,
  output out_6,
  output out_7,
  output out_8,
  output out_9,
  output out_10
);

  wire a_out, and_1_out, and_2_out, and_3_out, and_4_out, and_5_out, and_6_out, and_7_out, and_8_out,
       and_9_out, b_out, c_out, clock_1_out, clock_2_out, d_out, e_out, f_out, g_out, nand_1_out, not_1_out,
       not_2_out, not_3_out, not_4_out, not_5_out, not_6_out, not_7_out, t_ff_1_q, t_ff_2_q, t_ff_3_q,
       t_ff_4_q, t_ff_5_q, undriven;
  wire [1:0] nand_2_out;

  Clock clock_1 (.out(clock_1_out));
  Multiplexer multiplexer_1 (.in0(in_2), .in1(in_3), .out(out_6), .sel(nand_1_out));  // open: en
  T_Flip_Flop #(.trigger("falling")) t_ff_1 (
    .clk(clock_1_out), .T(out_6), .Q(t_ff_1_q));  // open: Qn, preset, reset, en
  Clock clock_2 (.out(clock_2_out));
  not not_1 (not_1_out, t_ff_1_q);
  Multiplexer #(.select(2)) multiplexer_2 (
    .in0(in_4), .in3(in_5), .out(out_7), .sel(nand_2_out), .en(nand_1_out));  // open: in1, in2
  T_Flip_Flop #(.trigger("falling")) t_ff_2 (
    .clk(clock_2_out), .T(out_7), .Q(t_ff_2_q), .Qn(out_10));  // open: preset, reset, en
  T_Flip_Flop #(.trigger("falling")) t_ff_3 (.clk(t_ff_1_q), .T(out_6), .Q(t_ff_3_q));  // open: Qn, preset, reset, en
  nand nand_1 (nand_1_out, t_ff_4_q, t_ff_3_q, not_1_out);
  T_Flip_Flop #(.trigger("falling")) t_ff_4 (.clk(t_ff_3_q), .T(out_6), .Q(t_ff_4_q));  // open: Qn, preset, reset, en
  not not_2 (not_2_out, nand_1_out);
  T_Flip_Flop #(.trigger("falling")) t_ff_5 (
    .clk(t_ff_2_q), .T(out_7), .Q(t_ff_5_q), .Qn(out_9), .preset(undriven));  // open: reset, en
  not not_3 (not_3_out, out_9);
  not not_4 (not_4_out, out_8);
  T_Flip_Flop #(.trigger("falling")) t_ff_6 (.clk(t_ff_5_q), .T(out_7), .Qn(out_8));  // open: Q, preset, reset, en
  nand nand_2 (nand_2_out[0], out_10, not_3_out, not_4_out);
  not not_5 (not_5_out, t_ff_4_q);
  not not_6 (not_6_out, t_ff_3_q);
  not not_7 (not_7_out, t_ff_1_q);
  and and_1 (and_1_out, not_7_out, t_ff_4_q);
  and and_2 (and_2_out, not_5_out, not_7_out);
  and and_3 (and_3_out, t_ff_1_q, t_ff_3_q);
  and and_4 (and_4_out, t_ff_1_q, t_ff_4_q);
  and and_5 (and_5_out, not_7_out, not_6_out);
  and and_6 (and_6_out, not_5_out, t_ff_3_q);
  and and_7 (and_7_out, t_ff_3_q, not_7_out);
  and and_8 (and_8_out, t_ff_4_q, not_6_out, t_ff_1_q);
  and and_9 (and_9_out, not_6_out, t_ff_4_q);
  or b (b_out, and_3_out, not_5_out, and_5_out);
  or c (c_out, not_6_out, t_ff_1_q, t_ff_4_q);
  or u_a (a_out, and_2_out, and_3_out, A, and_4_out);
  or d (d_out, and_2_out, and_6_out, and_7_out, and_8_out);
  or e (e_out, and_2_out, and_7_out);
  or f (f_out, and_5_out, and_9_out, and_1_out, A);
  or g (g_out, and_6_out, and_9_out, and_7_out, A);
  _7_Segment_Display u_7_segment_display_1 (
    .g(g_out), .f(f_out), .a(a_out), .b(b_out), .e(e_out), .d(d_out), .c(c_out));  // open: dp
  // Pins of 1 and 2 bits meet at nand_2_out

  // Notes on the sheet:
  //   A
  //   A
  //   B
  //   C
  //   B
  //   C
  //   B
  //   C
  //   D
endmodule
