// Logisim project 24 hrs clock.circ as structural Verilog: 1 circuit, main circuit main
module main (
  input  in_1,
  output out_2,
  output out_3,
  output out_4,
  output out_5,
  output out_6,
  output out_7,
  output out_8,
  output out_9,
  output out_10,
  output out_11,
  output out_12,
  output out_13,
  output out_14,
  output out_15,
  output out_16,
  output out_17,
  output out_18
);

  wire clock_1_out, nand_1_out, nand_2_out, nand_3_out, not_1_out, not_2_out, not_3_out, t_ff_1_qn,
       t_ff_2_qn, t_ff_3_qn, t_ff_6_qn, t_ff_7_qn, t_ff_12_qn, t_ff_13_qn;

  T_Flip_Flop #(.trigger("falling")) t_ff_1 (
    .clk(out_6), .T(in_1), .Q(out_5), .Qn(t_ff_1_qn), .reset(not_1_out));  // open: preset, en
  T_Flip_Flop #(.trigger("falling")) t_ff_2 (
    .clk(not_2_out), .T(in_1), .Q(out_6), .Qn(t_ff_2_qn), .reset(not_1_out));  // open: preset, en
  T_Flip_Flop #(.trigger("falling")) t_ff_3 (
    .clk(out_5), .T(in_1), .Q(out_4), .Qn(t_ff_3_qn), .reset(not_1_out));  // open: preset, en
  T_Flip_Flop #(.trigger("falling")) t_ff_4 (
    .clk(out_4), .T(in_1), .Q(out_3), .reset(not_1_out));  // open: Qn, preset, en
  nand nand_1 (nand_1_out, out_2, out_3, t_ff_3_qn, t_ff_1_qn, t_ff_2_qn);
  T_Flip_Flop #(.trigger("falling")) t_ff_5 (
    .clk(out_3), .T(in_1), .Q(out_2), .reset(not_1_out));  // open: Qn, preset, en
  not not_1 (not_1_out, nand_1_out);
  T_Flip_Flop #(.trigger("falling")) t_ff_6 (
    .clk(not_3_out), .T(in_1), .Q(out_12), .Qn(t_ff_6_qn), .reset(not_2_out));  // open: preset, en
  T_Flip_Flop #(.trigger("falling")) t_ff_7 (
    .clk(out_12), .T(in_1), .Q(out_11), .Qn(t_ff_7_qn), .reset(not_2_out));  // open: preset, en
  T_Flip_Flop #(.trigger("falling")) t_ff_8 (
    .clk(out_10), .T(in_1), .Q(out_9), .reset(not_2_out));  // open: Qn, preset, en
  T_Flip_Flop #(.trigger("falling")) t_ff_9 (
    .clk(out_11), .T(in_1), .Q(out_10), .reset(not_2_out));  // open: Qn, preset, en
  T_Flip_Flop #(.trigger("falling")) t_ff_10 (
    .clk(out_9), .T(in_1), .Q(out_8), .reset(not_2_out));  // open: Qn, preset, en
  not not_2 (not_2_out, nand_2_out);
  nand nand_2 (nand_2_out, t_ff_6_qn, t_ff_7_qn, out_10, out_9, out_8, out_7);
  T_Flip_Flop #(.trigger("falling")) t_ff_11 (
    .clk(out_8), .T(in_1), .Q(out_7), .reset(not_2_out));  // open: Qn, preset, en
  Clock clock_1 (.out(clock_1_out));
  T_Flip_Flop #(.trigger("falling")) t_ff_12 (
    .clk(clock_1_out), .T(in_1), .Q(out_18), .Qn(t_ff_12_qn), .reset(not_3_out));  // open: preset, en
  T_Flip_Flop #(.trigger("falling")) t_ff_13 (
    .clk(out_18), .T(in_1), .Q(out_17), .Qn(t_ff_13_qn), .reset(not_3_out));  // open: preset, en
  T_Flip_Flop #(.trigger("falling")) t_ff_14 (
    .clk(out_17), .T(in_1), .Q(out_16), .reset(not_3_out));  // open: Qn, preset, en
  T_Flip_Flop #(.trigger("falling")) t_ff_15 (
    .clk(out_16), .T(in_1), .Q(out_15), .reset(not_3_out));  // open: Qn, preset, en
  nand nand_3 (nand_3_out, t_ff_12_qn, t_ff_13_qn, out_16, out_15, out_14, out_13);
  T_Flip_Flop #(.trigger("falling")) t_ff_16 (
    .clk(out_15), .T(in_1), .Q(out_14), .reset(not_3_out));  // open: Qn, preset, en
  T_Flip_Flop #(.trigger("falling")) t_ff_17 (
    .clk(out_14), .T(in_1), .Q(out_13), .reset(not_3_out));  // open: Qn, preset, en
  not not_3 (not_3_out, nand_3_out);
endmodule
