// Logisim project 60 sec counter.circ as structural Verilog: 1 circuit, main circuit main
module main (
  input  in_1
);

  wire clock_1_out, nand_1_out, not_1_out, t_ff_1_q, t_ff_1_qn, t_ff_2_q, t_ff_2_qn, t_ff_3_q, t_ff_4_q,
       t_ff_5_q, t_ff_6_q;

  Clock clock_1 (.out(clock_1_out));
  T_Flip_Flop #(.trigger("falling")) t_ff_1 (
    .clk(clock_1_out), .T(in_1), .Q(t_ff_1_q), .Qn(t_ff_1_qn), .reset(not_1_out));  // open: preset, en
  T_Flip_Flop #(.trigger("falling")) t_ff_2 (
    .clk(t_ff_1_q), .T(in_1), .Q(t_ff_2_q), .Qn(t_ff_2_qn), .reset(not_1_out));  // open: preset, en
  T_Flip_Flop #(.trigger("falling")) t_ff_3 (
    .clk(t_ff_2_q), .T(in_1), .Q(t_ff_3_q), .reset(not_1_out));  // open: Qn, preset, en
  T_Flip_Flop #(.trigger("falling")) t_ff_4 (
    .clk(t_ff_3_q), .T(in_1), .Q(t_ff_4_q), .reset(not_1_out));  // open: Qn, preset, en
  nand nand_1 (nand_1_out, t_ff_1_qn, t_ff_2_qn, t_ff_3_q, t_ff_4_q, t_ff_5_q, t_ff_6_q);
  T_Flip_Flop #(.trigger("falling")) t_ff_5 (
    .clk(t_ff_4_q), .T(in_1), .Q(t_ff_5_q), .reset(not_1_out));  // open: Qn, preset, en
  T_Flip_Flop #(.trigger("falling")) t_ff_6 (
    .clk(t_ff_5_q), .T(in_1), .Q(t_ff_6_q), .reset(not_1_out));  // open: Qn, preset, en
  not not_1 (not_1_out, nand_1_out);
endmodule
