// Logisim project COUNTER.circ as structural Verilog: 1 circuit, main circuit main
module main (
  input  in_1,
  input  A,
  output out_3
);

  wire a_out, and_1_out, and_2_out, and_3_out, and_4_out, and_5_out, and_6_out, and_7_out, and_8_out,
       and_9_out, b_out, c_out, clock_1_out, d_out, e_out, f_out, g_out, not_1_out, not_2_out, not_3_out,
       t_ff_1_q, t_ff_2_q, undriven, undriven_2, undriven_3, undriven_4, undriven_5, undriven_6;

  Clock clock_1 (.out(clock_1_out));
  T_Flip_Flop #(.trigger("falling")) t_ff_1 (
    .clk(clock_1_out), .T(in_1), .Q(t_ff_1_q), .preset(undriven), .reset(undriven_2));  // open: Qn, en
  T_Flip_Flop #(.trigger("falling")) t_ff_2 (
    .clk(t_ff_1_q), .T(in_1), .Q(t_ff_2_q), .preset(undriven_3), .reset(undriven_4));  // open: Qn, en
  T_Flip_Flop #(.trigger("falling")) t_ff_3 (
    .clk(t_ff_2_q), .T(in_1), .Q(out_3), .preset(undriven_5), .reset(undriven_6));  // open: Qn, en
  not not_1 (not_1_out, out_3);
  not not_2 (not_2_out, t_ff_2_q);
  not not_3 (not_3_out, t_ff_1_q);
  and and_1 (and_1_out, not_3_out, out_3);
  and and_2 (and_2_out, not_1_out, not_3_out);
  and and_3 (and_3_out, t_ff_1_q, t_ff_2_q);
  and and_4 (and_4_out, t_ff_1_q, out_3);
  and and_5 (and_5_out, not_3_out, not_2_out);
  and and_6 (and_6_out, not_1_out, t_ff_2_q);
  and and_7 (and_7_out, t_ff_2_q, not_3_out);
  and and_8 (and_8_out, out_3, not_2_out, t_ff_1_q);
  and and_9 (and_9_out, not_2_out, out_3);
  or b (b_out, and_3_out, not_1_out, and_5_out);
  or c (c_out, not_2_out, t_ff_1_q, out_3);
  or u_a (a_out, and_2_out, and_3_out, A, and_4_out);
  or d (d_out, and_2_out, and_6_out, and_7_out, and_8_out);
  or e (e_out, and_2_out, and_7_out);
  or f (f_out, and_5_out, and_9_out, and_1_out, A);
  or g (g_out, and_6_out, and_9_out, and_7_out, A);
  _7_Segment_Display u_7_segment_display_1 (
    .g(g_out), .f(f_out), .a(a_out), .b(b_out), .e(e_out), .d(d_out), .c(c_out));  // open: dp

  // Notes on the sheet:
  //   A
  //   B
  //   C
  //   B
  //   C
  //   D
endmodule
