// Logisim project Clock 3.1.circ as structural Verilog: 1 circuit, main circuit main
module main (
  input  Start,
  input  in_2,
  input  in_3
);

  wire a_2_out, a_3_out, a_4_out, a_5_out, a_6_out, a_out, and_1_out, and_2_out, and_3_out, and_4_out,
       and_5_out, and_6_out, and_7_out, and_8_out, and_9_out, and_10_out, and_11_out, and_12_out, and_13_out,
       and_14_out, and_15_out, and_16_out, and_17_out, and_18_out, and_19_out, and_20_out, and_21_out,
       and_22_out, and_23_out, and_24_out, and_25_out, and_26_out, and_27_out, and_28_out, and_29_out,
       and_30_out, and_31_out, and_32_out, and_33_out, and_34_out, and_35_out, and_36_out, and_37_out,
       and_38_out, and_39_out, and_40_out, and_41_out, and_42_out, and_43_out, and_44_out, and_45_out,
       and_46_out, and_47_out, and_48_out, and_49_out, and_50_out, and_51_out, and_52_out, and_53_out,
       and_54_out, and_55_out, and_56_out, and_57_out, and_58_out, and_59_out, and_60_out, and_61_out,
       and_62_out, and_63_out, and_64_out, and_65_out, and_66_out, b_2_out, b_3_out, b_4_out, b_5_out,
       b_6_out, b_out, c_2_out, c_3_out, c_4_out, c_5_out, c_6_out, c_out, clock_1_out, d_2_out, d_3_out,
       d_4_out, d_5_out, d_6_out, d_out, e_2_out, e_3_out, e_4_out, e_5_out, e_6_out, e_out, f_2_out,
       f_3_out, f_4_out, f_5_out, f_6_out, f_out, g_2_out, g_3_out, g_4_out, g_5_out, g_6_out, g_out,
       not_1_out, not_2_out, not_3_out, not_4_out, not_5_out, not_6_out, not_7_out, not_8_out, not_9_out,
       not_10_out, not_11_out, not_12_out, not_13_out, not_14_out, not_15_out, not_16_out, not_17_out,
       not_18_out, not_19_out, not_20_out, not_21_out, not_22_out, or_1_out, t_ff_1_q, t_ff_1_qn, t_ff_2_q,
       t_ff_3_q, t_ff_3_qn, t_ff_4_q, t_ff_4_qn, t_ff_5_q, t_ff_5_qn, t_ff_6_q, t_ff_6_qn, t_ff_7_q,
       t_ff_7_qn, t_ff_8_q, t_ff_9_q, t_ff_10_q, t_ff_10_qn, t_ff_11_q, t_ff_12_q, t_ff_12_qn, t_ff_13_q,
       t_ff_14_q, t_ff_14_qn, t_ff_15_q, t_ff_16_q, t_ff_17_q, t_ff_17_qn, t_ff_18_q, t_ff_19_q, t_ff_19_qn,
       t_ff_20_q;

  not not_1 (not_1_out, in_3);
  not not_2 (not_2_out, t_ff_2_q);
  not not_3 (not_3_out, and_9_out);
  not not_4 (not_4_out, and_16_out);
  not not_5 (not_5_out, and_9_out);
  not not_6 (not_6_out, and_16_out);
  not not_7 (not_7_out, t_ff_1_q);
  T_Flip_Flop #(.trigger("falling")) t_ff_1 (
    .clk(or_1_out), .T(Start), .Q(t_ff_1_q), .Qn(t_ff_1_qn), .reset(and_15_out));  // open: preset, en
  and and_1 (and_1_out, not_3_out, and_17_out, not_4_out);
  and and_2 (and_2_out, not_5_out, and_17_out, and_16_out);
  and and_3 (and_3_out, and_9_out, and_17_out, not_6_out);
  and and_4 (and_4_out, and_9_out, in_2, and_16_out);
  and and_5 (and_5_out, not_1_out, t_ff_2_q);
  and and_6 (and_6_out, t_ff_2_q, not_7_out);
  and and_7 (and_7_out, in_3, not_2_out, t_ff_1_q);
  and and_8 (and_8_out, not_7_out, in_3);
  T_Flip_Flop #(.trigger("falling")) t_ff_2 (
    .clk(t_ff_1_q), .T(Start), .Q(t_ff_2_q), .reset(and_15_out));  // open: Qn, preset, en
  and and_9 (and_9_out, t_ff_2_q, t_ff_1_qn);
  and and_10 (and_10_out, not_1_out, not_7_out);
  and and_11 (and_11_out, t_ff_1_q, t_ff_2_q);
  and and_12 (and_12_out, t_ff_1_q, in_3);
  and and_13 (and_13_out, not_7_out, not_2_out);
  and and_14 (and_14_out, not_2_out, in_3);
  and and_15 (and_15_out, t_ff_2_q, t_ff_1_q);
  or or_1 (or_1_out, and_1_out, and_2_out, and_3_out, and_4_out);
  or a (a_out, and_10_out, and_11_out, in_3, and_12_out);
  or b (b_out, and_11_out, not_1_out, and_13_out);
  or c (c_out, not_2_out, t_ff_1_q, in_3);
  or d (d_out, and_10_out, and_5_out, and_6_out, and_7_out);
  or e (e_out, and_10_out, and_6_out);
  or f (f_out, and_13_out, and_14_out, and_8_out, in_3);
  or g (g_out, and_5_out, and_14_out, and_6_out, in_3);
  T_Flip_Flop #(.trigger("falling")) t_ff_3 (
    .clk(and_27_out), .T(Start), .Q(t_ff_3_q), .Qn(t_ff_3_qn), .reset(or_1_out));  // open: preset, en
  and and_16 (and_16_out, t_ff_6_qn, t_ff_5_q, t_ff_4_qn, t_ff_3_qn);
  T_Flip_Flop #(.trigger("falling")) t_ff_4 (
    .clk(t_ff_3_q), .T(Start), .Q(t_ff_4_q), .Qn(t_ff_4_qn), .reset(or_1_out));  // open: preset, en
  and and_17 (and_17_out, t_ff_6_q, t_ff_5_qn, t_ff_4_q, t_ff_3_qn);
  T_Flip_Flop #(.trigger("falling")) t_ff_5 (
    .clk(t_ff_4_q), .T(Start), .Q(t_ff_5_q), .Qn(t_ff_5_qn), .reset(or_1_out));  // open: preset, en
  not not_8 (not_8_out, t_ff_5_q);
  T_Flip_Flop #(.trigger("falling")) t_ff_6 (
    .clk(t_ff_5_q), .T(Start), .Q(t_ff_6_q), .Qn(t_ff_6_qn), .reset(or_1_out));  // open: preset, en
  not not_9 (not_9_out, t_ff_4_q);
  not not_10 (not_10_out, t_ff_3_q);
  and and_18 (and_18_out, not_10_out, t_ff_5_q);
  and and_19 (and_19_out, not_8_out, not_10_out);
  and and_20 (and_20_out, t_ff_3_q, t_ff_4_q);
  and and_21 (and_21_out, t_ff_3_q, t_ff_5_q);
  and and_22 (and_22_out, not_10_out, not_9_out);
  and and_23 (and_23_out, not_8_out, t_ff_4_q);
  and and_24 (and_24_out, t_ff_4_q, not_10_out);
  and and_25 (and_25_out, t_ff_5_q, not_9_out, t_ff_3_q);
  and and_26 (and_26_out, not_9_out, t_ff_5_q);
  or a_2 (a_2_out, and_19_out, and_20_out, t_ff_6_q, and_21_out);
  or b_2 (b_2_out, and_20_out, not_8_out, and_22_out);
  or c_2 (c_2_out, not_9_out, t_ff_3_q, t_ff_5_q);
  or d_2 (d_2_out, and_19_out, and_23_out, and_24_out, and_25_out);
  or e_2 (e_2_out, and_19_out, and_24_out);
  or g_2 (g_2_out, and_23_out, and_26_out, and_24_out, t_ff_6_q);
  or f_2 (f_2_out, and_22_out, and_26_out, and_18_out, t_ff_6_q);
  T_Flip_Flop #(.trigger("falling")) t_ff_7 (
    .clk(and_46_out), .T(Start), .Q(t_ff_7_q), .Qn(t_ff_7_qn), .reset(and_27_out));  // open: preset, en
  T_Flip_Flop #(.trigger("falling")) t_ff_8 (
    .clk(t_ff_7_q), .T(Start), .Q(t_ff_8_q), .reset(and_27_out));  // open: Qn, preset, en
  and and_27 (and_27_out, t_ff_9_q, t_ff_8_q, t_ff_7_qn);
  T_Flip_Flop #(.trigger("falling")) t_ff_9 (
    .clk(t_ff_8_q), .T(Start), .Q(t_ff_9_q), .reset(and_27_out));  // open: Qn, preset, en
  _7_Segment_Display u_7_segment_display_1 (
    .g(g_out), .f(f_out), .a(a_out), .b(b_out), .e(e_out), .d(d_out), .c(c_out));  // open: dp
  not not_11 (not_11_out, t_ff_9_q);
  not not_12 (not_12_out, t_ff_8_q);
  _7_Segment_Display u_7_segment_display_2 (
    .g(g_2_out), .f(f_2_out), .a(a_2_out), .b(b_2_out), .e(e_2_out), .d(d_2_out), .c(c_2_out));  // open: dp
  not not_13 (not_13_out, t_ff_7_q);
  _7_Segment_Display u_7_segment_display_3 (
    .g(g_3_out), .f(f_3_out), .a(a_3_out), .b(b_3_out), .e(e_3_out), .d(d_3_out), .c(c_3_out));  // open: dp
  and and_28 (and_28_out, not_13_out, not_12_out);
  and and_29 (and_29_out, not_11_out, t_ff_8_q);
  and and_30 (and_30_out, t_ff_8_q, not_13_out);
  and and_31 (and_31_out, t_ff_9_q, not_12_out, t_ff_7_q);
  and and_32 (and_32_out, not_13_out, t_ff_9_q);
  _7_Segment_Display u_7_segment_display_4 (
    .g(g_4_out), .f(f_4_out), .a(a_4_out), .b(b_4_out), .e(e_4_out), .d(d_4_out), .c(c_4_out));  // open: dp
  and and_33 (and_33_out, not_11_out, not_13_out);
  and and_34 (and_34_out, t_ff_7_q, t_ff_8_q);
  and and_35 (and_35_out, t_ff_7_q, t_ff_9_q);
  or b_3 (b_3_out, and_34_out, not_11_out, and_28_out);
  or c_3 (c_3_out, not_12_out, t_ff_7_q, t_ff_9_q);
  and and_36 (and_36_out, not_12_out, t_ff_9_q);
  or a_3 (a_3_out, and_33_out, and_34_out, in_3, and_35_out);
  or d_3 (d_3_out, and_33_out, and_29_out, and_30_out, and_31_out);
  or e_3 (e_3_out, and_33_out, and_30_out);
  or f_3 (f_3_out, and_28_out, and_36_out, and_32_out, in_3);
  or g_3 (g_3_out, and_29_out, and_36_out, and_30_out, in_3);
  _7_Segment_Display u_7_segment_display_5 (
    .g(g_5_out), .f(f_5_out), .a(a_5_out), .b(b_5_out), .e(e_5_out), .d(d_5_out), .c(c_5_out));  // open: dp
  _7_Segment_Display u_7_segment_display_6 (
    .g(g_6_out), .f(f_6_out), .a(a_6_out), .b(b_6_out), .e(e_6_out), .d(d_6_out), .c(c_6_out));  // open: dp
  not not_14 (not_14_out, t_ff_12_q);
  not not_15 (not_15_out, t_ff_11_q);
  not not_16 (not_16_out, t_ff_10_q);
  T_Flip_Flop #(.trigger("falling")) t_ff_10 (
    .clk(and_47_out), .T(Start), .Q(t_ff_10_q), .Qn(t_ff_10_qn), .reset(and_46_out));  // open: preset, en
  and and_37 (and_37_out, not_14_out, t_ff_11_q);
  and and_38 (and_38_out, t_ff_11_q, not_16_out);
  and and_39 (and_39_out, t_ff_12_q, not_15_out, t_ff_10_q);
  and and_40 (and_40_out, not_16_out, t_ff_12_q);
  T_Flip_Flop #(.trigger("falling")) t_ff_11 (
    .clk(t_ff_10_q), .T(Start), .Q(t_ff_11_q), .reset(and_46_out));  // open: Qn, preset, en
  and and_41 (and_41_out, not_14_out, not_16_out);
  and and_42 (and_42_out, t_ff_10_q, t_ff_11_q);
  and and_43 (and_43_out, t_ff_10_q, t_ff_12_q);
  and and_44 (and_44_out, not_16_out, not_15_out);
  and and_45 (and_45_out, not_15_out, t_ff_12_q);
  T_Flip_Flop #(.trigger("falling")) t_ff_12 (
    .clk(t_ff_11_q), .T(Start), .Q(t_ff_12_q), .Qn(t_ff_12_qn), .reset(and_46_out));  // open: preset, en
  and and_46 (and_46_out, t_ff_13_q, t_ff_12_qn, t_ff_11_q, t_ff_10_qn);
  or a_4 (a_4_out, and_41_out, and_42_out, t_ff_13_q, and_43_out);
  or b_4 (b_4_out, and_42_out, not_14_out, and_44_out);
  or c_4 (c_4_out, not_15_out, t_ff_10_q, t_ff_12_q);
  or d_4 (d_4_out, and_41_out, and_37_out, and_38_out, and_39_out);
  or e_4 (e_4_out, and_41_out, and_38_out);
  or g_4 (g_4_out, and_37_out, and_45_out, and_38_out, t_ff_13_q);
  T_Flip_Flop #(.trigger("falling")) t_ff_13 (
    .clk(t_ff_12_q), .T(Start), .Q(t_ff_13_q), .reset(and_46_out));  // open: Qn, preset, en
  or f_4 (f_4_out, and_44_out, and_45_out, and_40_out, t_ff_13_q);
  T_Flip_Flop #(.trigger("falling")) t_ff_14 (
    .clk(and_57_out), .T(Start), .Q(t_ff_14_q), .Qn(t_ff_14_qn), .reset(and_47_out));  // open: preset, en
  T_Flip_Flop #(.trigger("falling")) t_ff_15 (
    .clk(t_ff_14_q), .T(Start), .Q(t_ff_15_q), .reset(and_47_out));  // open: Qn, preset, en
  T_Flip_Flop #(.trigger("falling")) t_ff_16 (
    .clk(t_ff_15_q), .T(Start), .Q(t_ff_16_q), .reset(and_47_out));  // open: Qn, preset, en
  and and_47 (and_47_out, t_ff_16_q, t_ff_15_q, t_ff_14_qn);
  not not_17 (not_17_out, t_ff_16_q);
  not not_18 (not_18_out, t_ff_15_q);
  not not_19 (not_19_out, t_ff_14_q);
  and and_48 (and_48_out, not_19_out, t_ff_16_q);
  and and_49 (and_49_out, not_17_out, not_19_out);
  and and_50 (and_50_out, t_ff_14_q, t_ff_15_q);
  and and_51 (and_51_out, t_ff_14_q, t_ff_16_q);
  and and_52 (and_52_out, not_19_out, not_18_out);
  and and_53 (and_53_out, not_17_out, t_ff_15_q);
  and and_54 (and_54_out, t_ff_15_q, not_19_out);
  and and_55 (and_55_out, t_ff_16_q, not_18_out, t_ff_14_q);
  and and_56 (and_56_out, not_18_out, t_ff_16_q);
  Clock clock_1 (.out(clock_1_out));
  or a_5 (a_5_out, and_49_out, and_50_out, in_3, and_51_out);
  or b_5 (b_5_out, and_50_out, not_17_out, and_52_out);
  or c_5 (c_5_out, not_18_out, t_ff_14_q, t_ff_16_q);
  or d_5 (d_5_out, and_49_out, and_53_out, and_54_out, and_55_out);
  or e_5 (e_5_out, and_49_out, and_54_out);
  or f_5 (f_5_out, and_52_out, and_56_out, and_48_out, in_3);
  or g_5 (g_5_out, and_53_out, and_56_out, and_54_out, in_3);
  T_Flip_Flop #(.trigger("falling")) t_ff_17 (
    .clk(clock_1_out), .T(Start), .Q(t_ff_17_q), .Qn(t_ff_17_qn), .reset(and_57_out));  // open: preset, en
  T_Flip_Flop #(.trigger("falling")) t_ff_18 (
    .clk(t_ff_17_q), .T(Start), .Q(t_ff_18_q), .reset(and_57_out));  // open: Qn, preset, en
  and and_57 (and_57_out, t_ff_20_q, t_ff_19_qn, t_ff_18_q, t_ff_17_qn);
  T_Flip_Flop #(.trigger("falling")) t_ff_19 (
    .clk(t_ff_18_q), .T(Start), .Q(t_ff_19_q), .Qn(t_ff_19_qn), .reset(and_57_out));  // open: preset, en
  T_Flip_Flop #(.trigger("falling")) t_ff_20 (
    .clk(t_ff_19_q), .T(Start), .Q(t_ff_20_q), .reset(and_57_out));  // open: Qn, preset, en
  not not_20 (not_20_out, t_ff_19_q);
  not not_21 (not_21_out, t_ff_18_q);
  not not_22 (not_22_out, t_ff_17_q);
  and and_58 (and_58_out, not_20_out, t_ff_18_q);
  and and_59 (and_59_out, t_ff_18_q, not_22_out);
  and and_60 (and_60_out, t_ff_19_q, not_21_out, t_ff_17_q);
  and and_61 (and_61_out, not_22_out, t_ff_19_q);
  and and_62 (and_62_out, not_20_out, not_22_out);
  and and_63 (and_63_out, t_ff_17_q, t_ff_18_q);
  and and_64 (and_64_out, t_ff_17_q, t_ff_19_q);
  and and_65 (and_65_out, not_22_out, not_21_out);
  and and_66 (and_66_out, not_21_out, t_ff_19_q);
  or a_6 (a_6_out, and_62_out, and_63_out, t_ff_20_q, and_64_out);
  or b_6 (b_6_out, and_63_out, not_20_out, and_65_out);
  or c_6 (c_6_out, not_21_out, t_ff_17_q, t_ff_19_q);
  or d_6 (d_6_out, and_62_out, and_58_out, and_59_out, and_60_out);
  or e_6 (e_6_out, and_62_out, and_59_out);
  or f_6 (f_6_out, and_65_out, and_66_out, and_61_out, t_ff_20_q);
  or g_6 (g_6_out, and_58_out, and_66_out, and_59_out, t_ff_20_q);

  // Notes on the sheet:
  //   A
  //   2  4
  //   B
  //   C
  //   D
  //   B
  //   A
  //   C
  //   D
  //   A
  //   C
  //   B
  //   D
  //   O
  //   O
  //   24 Hrs Clock
  //   @ShlokPandey
  //   O
  //   O
  //   A
  //   B
  //   C
  //   D
  //   B
  //   A
  //   C
  //   D
  //   A
  //   C
  //   B
  //   D
endmodule
