// Logisim project Counter till 999(Raw).circ as structural Verilog: 1 circuit, main circuit main
module main (
  input  in_1
);

  wire a_2_out, a_3_out, a_out, and_1_out, and_2_out, and_3_out, and_4_out, and_5_out, and_6_out, and_7_out,
       and_8_out, and_9_out, and_10_out, and_11_out, and_12_out, and_13_out, and_14_out, and_15_out,
       and_16_out, and_17_out, and_18_out, and_19_out, and_20_out, and_21_out, and_22_out, and_23_out,
       and_24_out, and_25_out, and_26_out, and_27_out, and_28_out, and_29_out, and_30_out, b_2_out, b_3_out,
       b_out, c_2_out, c_3_out, c_out, clock_1_out, d_2_out, d_3_out, d_out, e_2_out, e_3_out, e_out,
       f_2_out, f_3_out, f_out, g_2_out, g_3_out, g_out, not_1_out, not_2_out, not_3_out, not_4_out,
       not_5_out, not_6_out, not_7_out, not_8_out, not_9_out, t_ff_1_q, t_ff_1_qn, t_ff_2_q, t_ff_3_q,
       t_ff_3_qn, t_ff_4_q, t_ff_5_q, t_ff_5_qn, t_ff_6_q, t_ff_7_q, t_ff_7_qn, t_ff_8_q, t_ff_9_q,
       t_ff_9_qn, t_ff_10_q, t_ff_11_q, t_ff_11_qn, t_ff_12_q;

  not not_1 (not_1_out, t_ff_3_q);
  not not_2 (not_2_out, t_ff_2_q);
  not not_3 (not_3_out, t_ff_1_q);
  T_Flip_Flop #(.trigger("falling")) t_ff_1 (
    .clk(and_11_out), .T(in_1), .Q(t_ff_1_q), .Qn(t_ff_1_qn), .reset(and_10_out));  // open: preset, en
  and and_1 (and_1_out, not_1_out, t_ff_2_q);
  and and_2 (and_2_out, t_ff_2_q, not_3_out);
  and and_3 (and_3_out, t_ff_3_q, not_2_out, t_ff_1_q);
  and and_4 (and_4_out, not_3_out, t_ff_3_q);
  T_Flip_Flop #(.trigger("falling")) t_ff_2 (
    .clk(t_ff_1_q), .T(in_1), .Q(t_ff_2_q), .reset(and_10_out));  // open: Qn, preset, en
  and and_5 (and_5_out, not_1_out, not_3_out);
  and and_6 (and_6_out, t_ff_1_q, t_ff_2_q);
  and and_7 (and_7_out, t_ff_1_q, t_ff_3_q);
  and and_8 (and_8_out, not_3_out, not_2_out);
  and and_9 (and_9_out, not_2_out, t_ff_3_q);
  T_Flip_Flop #(.trigger("falling")) t_ff_3 (
    .clk(t_ff_2_q), .T(in_1), .Q(t_ff_3_q), .Qn(t_ff_3_qn), .reset(and_10_out));  // open: preset, en
  and and_10 (and_10_out, t_ff_4_q, t_ff_3_qn, t_ff_2_q, t_ff_1_qn);
  or a (a_out, and_5_out, and_6_out, t_ff_4_q, and_7_out);
  or b (b_out, and_6_out, not_1_out, and_8_out);
  or c (c_out, not_2_out, t_ff_1_q, t_ff_3_q);
  or d (d_out, and_5_out, and_1_out, and_2_out, and_3_out);
  or e (e_out, and_5_out, and_2_out);
  or f (f_out, and_8_out, and_9_out, and_4_out, t_ff_4_q);
  or g (g_out, and_1_out, and_9_out, and_2_out, t_ff_4_q);
  T_Flip_Flop #(.trigger("falling")) t_ff_4 (
    .clk(t_ff_3_q), .T(in_1), .Q(t_ff_4_q), .reset(and_10_out));  // open: Qn, preset, en
  _7_Segment_Display u_7_segment_display_1 (
    .g(g_out), .f(f_out), .a(a_out), .b(b_out), .e(e_out), .d(d_out), .c(c_out));  // open: dp
  T_Flip_Flop #(.trigger("falling")) t_ff_5 (
    .clk(and_21_out), .T(in_1), .Q(t_ff_5_q), .Qn(t_ff_5_qn), .reset(and_11_out));  // open: preset, en
  T_Flip_Flop #(.trigger("falling")) t_ff_6 (
    .clk(t_ff_5_q), .T(in_1), .Q(t_ff_6_q), .reset(and_11_out));  // open: Qn, preset, en
  and and_11 (and_11_out, t_ff_8_q, t_ff_7_qn, t_ff_6_q, t_ff_5_qn);
  T_Flip_Flop #(.trigger("falling")) t_ff_7 (
    .clk(t_ff_6_q), .T(in_1), .Q(t_ff_7_q), .Qn(t_ff_7_qn), .reset(and_11_out));  // open: preset, en
  not not_4 (not_4_out, t_ff_7_q);
  T_Flip_Flop #(.trigger("falling")) t_ff_8 (
    .clk(t_ff_7_q), .T(in_1), .Q(t_ff_8_q), .reset(and_11_out));  // open: Qn, preset, en
  not not_5 (not_5_out, t_ff_6_q);
  not not_6 (not_6_out, t_ff_5_q);
  and and_12 (and_12_out, not_6_out, t_ff_7_q);
  Clock clock_1 (.out(clock_1_out));
  and and_13 (and_13_out, not_4_out, not_6_out);
  and and_14 (and_14_out, t_ff_5_q, t_ff_6_q);
  and and_15 (and_15_out, t_ff_5_q, t_ff_7_q);
  and and_16 (and_16_out, not_6_out, not_5_out);
  and and_17 (and_17_out, not_4_out, t_ff_6_q);
  and and_18 (and_18_out, t_ff_6_q, not_6_out);
  and and_19 (and_19_out, t_ff_7_q, not_5_out, t_ff_5_q);
  and and_20 (and_20_out, not_5_out, t_ff_7_q);
  or a_2 (a_2_out, and_13_out, and_14_out, t_ff_8_q, and_15_out);
  or b_2 (b_2_out, and_14_out, not_4_out, and_16_out);
  or c_2 (c_2_out, not_5_out, t_ff_5_q, t_ff_7_q);
  or d_2 (d_2_out, and_13_out, and_17_out, and_18_out, and_19_out);
  or e_2 (e_2_out, and_13_out, and_18_out);
  or g_2 (g_2_out, and_17_out, and_20_out, and_18_out, t_ff_8_q);
  or f_2 (f_2_out, and_16_out, and_20_out, and_12_out, t_ff_8_q);
  T_Flip_Flop #(.trigger("falling")) t_ff_9 (
    .clk(clock_1_out), .T(in_1), .Q(t_ff_9_q), .Qn(t_ff_9_qn), .reset(and_21_out));  // open: preset, en
  T_Flip_Flop #(.trigger("falling")) t_ff_10 (
    .clk(t_ff_9_q), .T(in_1), .Q(t_ff_10_q), .reset(and_21_out));  // open: Qn, preset, en
  and and_21 (and_21_out, t_ff_12_q, t_ff_11_qn, t_ff_10_q, t_ff_9_qn);
  T_Flip_Flop #(.trigger("falling")) t_ff_11 (
    .clk(t_ff_10_q), .T(in_1), .Q(t_ff_11_q), .Qn(t_ff_11_qn), .reset(and_21_out));  // open: preset, en
  _7_Segment_Display u_7_segment_display_2 (
    .g(g_2_out), .f(f_2_out), .a(a_2_out), .b(b_2_out), .e(e_2_out), .d(d_2_out), .c(c_2_out));  // open: dp
  T_Flip_Flop #(.trigger("falling")) t_ff_12 (
    .clk(t_ff_11_q), .T(in_1), .Q(t_ff_12_q), .reset(and_21_out));  // open: Qn, preset, en
  not not_7 (not_7_out, t_ff_11_q);
  not not_8 (not_8_out, t_ff_10_q);
  not not_9 (not_9_out, t_ff_9_q);
  and and_22 (and_22_out, not_9_out, not_8_out);
  and and_23 (and_23_out, not_7_out, t_ff_10_q);
  and and_24 (and_24_out, t_ff_10_q, not_9_out);
  and and_25 (and_25_out, t_ff_11_q, not_8_out, t_ff_9_q);
  and and_26 (and_26_out, not_9_out, t_ff_11_q);
  and and_27 (and_27_out, not_7_out, not_9_out);
  and and_28 (and_28_out, t_ff_9_q, t_ff_10_q);
  and and_29 (and_29_out, t_ff_9_q, t_ff_11_q);
  or b_3 (b_3_out, and_28_out, not_7_out, and_22_out);
  or c_3 (c_3_out, not_8_out, t_ff_9_q, t_ff_11_q);
  and and_30 (and_30_out, not_8_out, t_ff_11_q);
  or a_3 (a_3_out, and_27_out, and_28_out, t_ff_12_q, and_29_out);
  or d_3 (d_3_out, and_27_out, and_23_out, and_24_out, and_25_out);
  or e_3 (e_3_out, and_27_out, and_24_out);
  or f_3 (f_3_out, and_22_out, and_30_out, and_26_out, t_ff_12_q);
  or g_3 (g_3_out, and_23_out, and_30_out, and_24_out, t_ff_12_q);
  _7_Segment_Display u_7_segment_display_3 (
    .g(g_3_out), .f(f_3_out), .a(a_3_out), .b(b_3_out), .e(e_3_out), .d(d_3_out), .c(c_3_out));  // open: dp

  // Notes on the sheet:
  //   A
  //   B
  //   C
  //   D
  //   B
  //   A
  //   C
  //   D
  //   A
  //   C
  //   B
  //   D
endmodule
