// Logisim project Ring Counter.circ as structural Verilog: 1 circuit, main circuit main
module main (
  input  in_1,
  output out_2,
  output out_3,
  output out_4,
  output out_5
);

  wire clock_1_out;

  Clock clock_1 (.out(clock_1_out));
  D_Flip_Flop d_ff_1 (.clk(clock_1_out), .D(out_5), .Q(out_2), .preset(in_1));  // open: Qn, en, reset
  D_Flip_Flop d_ff_2 (.clk(clock_1_out), .D(out_2), .Q(out_3), .reset(in_1));  // open: Qn, preset, en
  D_Flip_Flop d_ff_3 (.clk(clock_1_out), .D(out_3), .Q(out_4), .reset(in_1));  // open: Qn, preset, en
  D_Flip_Flop d_ff_4 (.clk(clock_1_out), .D(out_4), .Q(out_5), .reset(in_1));  // open: Qn, preset, en
endmodule
