// Logisim project IC test misc.circ as structural Verilog: 2 circuits, main circuit main
module main (
  input  in_1,
  input  in_2,
  input  in_3,
  input  in_4,
  input  in_5,
  input  in_6,
  input  in_7,
  input  in_8,
  output out_9,
  output out_10,
  output out_11,
  output out_12
);

  nand nand_1 (out_9, in_2, in_1);
  nand nand_2 (out_11, in_5, in_6);
  nand nand_3 (out_10, in_4, in_3);
  nand nand_4 (out_12, in_7, in_8);
endmodule

module \new  (
  input  in_1,
  input  in_2,
  output out_3
);

  main main_1 (
    .out_11(out_3), .in_5(in_1), .in_6(in_2), .in_7(out_3), .in_8(out_3), .out_12(out_3), .out_9(out_3),
    .in_3(out_3), .in_4(out_3), .out_10(out_3));  // open: in_1, in_2
endmodule
