// Logisim project adder Misc.circ as structural Verilog: 1 circuit, main circuit main
module main (
  input  in_1,
  input  in_2,
  input  in_3,
  input  in_4,
  output out_5,
  output out_6,
  output out_7,
  output out_8
);

  wire and_1_out, and_2_out, and_3_out, and_4_out, undriven;

  xor xor_1 (out_5, in_1, and_2_out);
  and and_1 (and_1_out, and_2_out, in_1);
  and and_2 (and_2_out, and_3_out, in_2);
  xor xor_2 (out_6, in_2, and_3_out);
  xor xor_3 (out_7, in_3, and_4_out);
  and and_3 (and_3_out, and_4_out, in_3);
  xor xor_4 (out_8, in_4, undriven);
  and and_4 (and_4_out, undriven, in_4);
endmodule
