// Logisim project adder.circ as structural Verilog
module main (
  input  in_1,
  input  in_2,
  output out_3,
  output out_4
);

  xor xor_1 (out_3, in_1, in_2);
  and and_1 (out_4, in_1, in_2);
endmodule

module Half_Adder (
  input  in_1,
  input  in_2,
  input  in_3,
  output out_4,
  output out_5,
  output out_6
);

  wire main_1_out_4;

  main main_1 (.in_1(in_1), .in_2(in_2), .out_3(out_4), .out_4(main_1_out_4));
  main main_2 (.in_1(main_1_out_4), .in_2(in_3), .out_3(out_5), .out_4(out_6));
endmodule
