// Logisim project half and full adders.circ as structural Verilog
module halfadd (
  input  in_1,
  input  in_2,
  output out_3,
  output out_4
);

  xor xor_1 (out_3, in_1, in_2);
  and and_1 (out_4, in_1, in_2);
endmodule

module fulladd (
  input  in_1,
  input  in_2,
  input  in_3,
  output out_4,
  output out_5
);

  wire halfadd_1_out_3, halfadd_1_out_4, halfadd_2_out_4;

  halfadd halfadd_1 (.in_1(in_1), .in_2(in_2), .out_3(halfadd_1_out_3), .out_4(halfadd_1_out_4));
  halfadd halfadd_2 (.in_1(halfadd_1_out_3), .in_2(in_3), .out_3(out_4), .out_4(halfadd_2_out_4));
  or or_1 (out_5, halfadd_2_out_4, halfadd_1_out_4);
endmodule
