// Logisim project seven segment display.circ as structural Verilog: 1 circuit, main circuit main
module main (
  input  A,
  input  B,
  input  C,
  input  D
);

  wire a_out, and_1_out, and_2_out, and_3_out, and_4_out, and_5_out, and_6_out, and_7_out, and_8_out,
       and_9_out, b_out, c_out, d_out, e_out, f_out, g_out, not_1_out, not_2_out, not_3_out;

  not not_1 (not_1_out, B);
  not not_2 (not_2_out, C);
  not not_3 (not_3_out, D);
  and and_1 (and_1_out, not_1_out, C);
  and and_2 (and_2_out, C, not_3_out);
  and and_3 (and_3_out, B, not_2_out, D);
  and and_4 (and_4_out, not_3_out, B);
  and and_5 (and_5_out, not_1_out, not_3_out);
  and and_6 (and_6_out, D, C);
  and and_7 (and_7_out, D, B);
  and and_8 (and_8_out, not_3_out, not_2_out);
  and and_9 (and_9_out, not_2_out, B);
  or u_a (a_out, and_5_out, and_6_out, A, and_7_out);
  or u_b (b_out, and_6_out, not_1_out, and_8_out);
  or u_c (c_out, not_2_out, D, B);
  or u_d (d_out, and_5_out, and_1_out, and_2_out, and_3_out);
  or e (e_out, and_5_out, and_2_out);
  or f (f_out, and_8_out, and_9_out, and_4_out, A);
  or g (g_out, and_1_out, and_9_out, and_2_out, A);
  _7_Segment_Display u_7_segment_display_1 (
    .g(g_out), .f(f_out), .a(a_out), .b(b_out), .e(e_out), .d(d_out), .c(c_out));  // open: dp
endmodule
