// Logisim project testlatch misc.circ as structural Verilog: 1 circuit, main circuit main
module main (
  input  D,
  input  En,
  input  R,
  input  S,
  output out_5,
  output Q,
  output Q_prime,
  output Q_2,
  output Q_prime_2
);

  wire nand_1_out, nand_2_out, not_1_out;

  not not_1 (not_1_out, D);
  nand nand_1 (nand_1_out, D, En);
  nand nand_2 (nand_2_out, En, not_1_out);
  nand nand_3 (Q, nand_1_out, Q_prime);
  nand nand_4 (Q_prime, Q, nand_2_out);
  nor nor_1 (Q_2, R, Q_prime_2);
  nor nor_2 (Q_prime_2, Q_2, S);
  D_Flip_Flop d_ff_1 (.clk(En), .D(D), .Q(out_5));  // open: Qn, preset, en, reset

  // Notes on the sheet:
  //   D'
  //   S* = D' + En'
  //   R* = D + En'
endmodule
